# Fritzing sketch BT-HC06-LED-SS (saved by Fritzing 0.9.3b)
breadboards: 1

parts:
  BT1 = Bluetooth HC-06u [package=THT]
  Componente1 = Arduino Uno (Rev3)
  LED1 = LED - 5mm [color="Red (633nm)" package="5 mm [THT]"]
  R1 = Resistor [tolerance=±5% resistance=220 package=THT]

nets:
  VCC: BT1.VCC, Componente1.5V
  GND: BT1.GND, Componente1.GND, R1.Pin_1
  N1: BT1.TXD, Componente1.D10_PWM/SS
  N2: BT1.RXD, Componente1.D11_PWM/MOSI
  N3: Componente1.D13/SCK, LED1.anode
  N4: LED1.cathode, R1.Pin_0

custom parts:
  Bluetooth HC-06u: Bluetooth HC-06 - face up, pins down 16.5mm x 37.5mm PCB
