# Fritzing sketch Bluetooth-LED-SS (saved by Fritzing 0.9.2b)

parts:
  Parte2 = Arduino Uno (Rev3)
  Parte4 = Bluetooth HC-06
  LED1 = LED - 5mm [color="Red (633nm)" package="5 mm [THT]"]
  R1 = Resistor [tolerance=±5% resistance=220 package=THT]

nets:
  N1: Parte2.D10_PWM/SS, Parte4.TXD
  N2: Parte2.D11_PWM/MOSI, Parte4.RXD
  N3: Parte2.D13/SCK, LED1.anode
  GND: Parte2.GND, Parte4.GND, R1.Pin_1
  5V: Parte2.5V, Parte4.VCC
