# Fritzing sketch BT-HC06-Servo (saved by Fritzing 0.9.3b)
breadboards: 1

parts:
  BT1 = Bluetooth HC-06u [package=THT]
  Componente1 = Arduino Uno (Rev3)
  J1 = Basic Servo

nets:
  VCC: BT1.VCC, Componente1.5V, J1.vcc
  GND: BT1.GND, Componente1.GND, J1.gnd
  N1: BT1.TXD, Componente1.D0/RX
  N2: BT1.RXD, Componente1.D1/TX
  N3: Componente1.D9_PWM, J1.pulse

custom parts:
  Bluetooth HC-06u: Bluetooth HC-06 - face up, pins down 16.5mm x 37.5mm PCB
