# Fritzing sketch Bluetooth-Servo-SS (saved by Fritzing 0.9.3b)
breadboards: 1

parts:
  Parte2 = Arduino Uno (Rev3)
  Parte4 = Bluetooth HC-06
  J1 = Basic Servo

nets:
  N1: Parte2.D9_PWM, J1.pulse
  N2: Parte2.D10_PWM/SS, Parte4.TXD
  N3: Parte2.D11_PWM/MOSI, Parte4.RXD
  GND: Parte2.GND, Parte4.GND, J1.gnd
  VCC: Parte2.5V, Parte4.VCC, J1.vcc
