# Fritzing sketch Bluetooth-Servo (saved by Fritzing 0.9.3b)
breadboards: 1

parts:
  Parte2 = Arduino Uno (Rev3)
  Parte4 = Bluetooth HC-06
  J1 = Basic Servo

nets:
  N1: Parte2.D9_PWM, J1.pulse
  GND: Parte2.GND, Parte4.GND, J1.gnd
  N2: Parte2.D0/RX, Parte4.TXD
  N3: Parte2.D1/TX, Parte4.RXD
  VCC: Parte2.5V, Parte4.VCC, J1.vcc
