# Fritzing sketch BT-HC06-LM35 (saved by Fritzing 0.9.3b)
breadboards: 1

parts:
  BT1 = Bluetooth HC-06u [package=THT]
  Componente1 = Arduino Uno (Rev3)
  T1 = LM35 Temperature Sensor [package="TO92 [THT]"]

nets:
  VCC: BT1.VCC, Componente1.5V, T1.+Vs
  GND: BT1.GND, Componente1.GND, T1.GND
  N1: BT1.TXD, Componente1.D0/RX
  N2: BT1.RXD, Componente1.D1/TX
  N3: Componente1.A0, T1.Vout

custom parts:
  Bluetooth HC-06u: Bluetooth HC-06 - face up, pins down 16.5mm x 37.5mm PCB
