# Fritzing sketch Bluetooth-Temp (saved by Fritzing 0.9.3b)
breadboards: 1

parts:
  Parte2 = Arduino Uno (Rev3)
  Parte4 = Bluetooth HC-06
  T1 = LM35 Temperature Sensor [package="TO92 [THT]"]

nets:
  N1: Parte2.A0, T1.Vout
  N2: Parte2.D0/RX, Parte4.TXD
  N3: Parte2.D1/TX, Parte4.RXD
  5V: Parte2.5V, Parte4.VCC, T1.+Vs
  GND: Parte2.GND, Parte4.GND, T1.GND
